# Fritzing sketch Armic (saved by Fritzing 0.9.6b)

parts:
  A1 = HW-688
  J1 = Basic Servo
  J2 = Basic Servo
  J3 = Basic Servo
  J4 = Basic Servo
  J5 = Basic Servo
  Power_plug1 = Power plug
  Part1 = Adafruit PCA9685 PWM/Servo Breakout [part_number=815]

nets:
  N1: A1.Pin_3, Power_plug1.VCC
  GND: A1.Pin_4, A1.Pin_5, J1.gnd, Power_plug1.GND, Part1.GND
  N2: A1.Pin_6, Part1.PWRIN
  N3: J1.vcc, Part1.5.0V
  N4: J1.pulse, Part1.PWM0
  N5: J2.pulse, Part1.PWM3
  N6: J3.pulse, Part1.PWM2
  N7: J4.pulse, Part1.PWM1
  N8: J5.pulse, Part1.PWM4

notes:
  12V - 5A
  Base
  Shoulder
  Elbow
  Wrist
  Claw

custom parts:
  HW-688: DC-DC 24V/12V To 5V 5A Step Down Power Supply Buck Converter.
  Adafruit PCA9685 PWM/Servo Breakout: Using only two pins, control 16 free-running PWM outputs! I2C-controlled PWM driver with a built in clock. Unlike the TLC5940 family, you do not need to continuously send it signal tying up your microcontroller, its completely free running! 5V compliant, which means you can control it from a 3.3V microcontroller and still safely drive up to 6V outputs (this is good for when you want to control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
